// Logisim project Project2Given.circ as structural Verilog: 4 circuits, main circuit main
module main (
);

  wire and_1_out, and_2_out, B0, B1, B2, B3, B4, B5, B6, B7, B8, B9, BL, BU, C0, C1, C2, CLK, L1_l, L1_u,
       not_1_out, or_8_out, P1_v, R0, R1, R3, R4, Valid;
  wire [2:0] counter_1_q;
  wire [3:0] IB1_c0, P1_b0, register_3_q, register_4_q, register_5_q;

  Button n1 (.out(B1));
  Button n4 (.out(B4));
  Button n7 (.out(B7));
  Button L (.out(BL));
  Button n3 (.out(B3));
  Button n2 (.out(B2));
  Button n6 (.out(B6));
  Button n5 (.out(B5));
  Button n9 (.out(B9));
  Button n8 (.out(B8));
  Button U (.out(BU));
  Button n0 (.out(B0));
  or or_1 (R0, B3, B2, B1);
  or or_2 (R1, B6, B5, B4);
  or or_3 (R3, B9, B8, B7);
  or or_4 (R4, BU, B0, BL);
  or or_5 (C0, B1, B4, B7, BL);
  or or_6 (C1, B2, B5, B8, B0);
  or or_7 (C2, B3, B6, B9, BU);
  Clock clock_1 (.out(CLK));
  nand nand_1 (Valid, IB1_c0[0], IB1_c0[1], IB1_c0[2], IB1_c0[3]);
  // Probe on P1_b0
  Panel P1 (
    .R0(R0), .R1(R1), .R2(R3), .R3(R4), .C0(C0), .C1(C1), .C2(C2), .B0(P1_b0[0]), .B1(P1_b0[1]),
    .B2(P1_b0[2]), .B3(P1_b0[3]), .V(P1_v));
  LED Press (.in(P1_v));
  // Probe on IB1_c0
  InputBuffer IB1 (
    .B0(P1_b0[0]), .B1(P1_b0[1]), .B2(P1_b0[2]), .B3(P1_b0[3]), .V(P1_v), .CLK(not_1_out), .C0(IB1_c0[0]),
    .C1(IB1_c0[1]), .C2(IB1_c0[2]), .C3(IB1_c0[3]));
  not not_1 (not_1_out, CLK);
  Register #(.width(4)) register_1 (.D(register_3_q), .en(Valid), .clk(CLK));  // open: Q, clr
  Lock L1 (.C0(IB1_c0[0]), .C1(IB1_c0[1]), .C2(IB1_c0[2]), .C3(IB1_c0[3]), .CLK(CLK), .L(L1_l), .U(L1_u));
  Counter #(.max('h7), .width(3)) counter_1 (
    .count(or_8_out), .Q(counter_1_q), .up(L1_u), .clk(CLK));  // open: load, D, carry, clr
  or or_8 (or_8_out, L1_l, L1_u);
  Register #(.width(4)) register_2 (.D(register_3_q), .en(Valid), .clk(CLK));  // open: Q, clr
  LED Unlocked (.in(and_1_out));
  and and_1 (and_1_out, ~counter_1_q[0], ~counter_1_q[1], ~counter_1_q[2]);  // AND_Gate
  Register #(.width(4)) register_3 (.D(register_4_q), .en(Valid), .clk(CLK), .Q(register_3_q));  // open: clr
  LED Locked (.in(and_2_out));
  and and_2 (and_2_out, ~counter_1_q[0], ~counter_1_q[1], counter_1_q[2]);  // AND_Gate
  Register #(.width(4)) register_4 (.D(register_5_q), .en(Valid), .clk(CLK), .Q(register_4_q));  // open: clr
  Register #(.width(4)) register_5 (.D(IB1_c0), .en(Valid), .clk(CLK), .Q(register_5_q));  // open: clr
endmodule

module Panel (
  input  R0,
  input  R1,
  input  R2,
  input  R3,
  input  C0,
  input  C1,
  input  C2,
  output B0,
  output B1,
  output B2,
  output B3,
  output V
);

  wire and_1_out, and_2_out, and_3_out, and_4_out, and_5_out, and_6_out, and_7_out, and_8_out, and_9_out,
       and_10_out, and_11_out, and_12_out, and_13_out, and_14_out, and_15_out, and_16_out, and_17_out,
       and_18_out, and_19_out, and_21_out, and_22_out, and_23_out, and_24_out, and_25_out, and_26_out,
       and_27_out, and_28_out, not_1_out, not_2_out, not_3_out, not_4_out, not_5_out, not_6_out, not_7_out,
       not_8_out, not_9_out, not_10_out, not_11_out, not_12_out, not_13_out, not_14_out, or_2_out, or_3_out;

  not not_1 (not_1_out, R0);
  not not_2 (not_2_out, R1);
  not not_3 (not_3_out, R2);
  not not_4 (not_4_out, R3);
  not not_5 (not_5_out, C0);
  not not_6 (not_6_out, C1);
  not not_7 (not_7_out, C2);
  not not_8 (not_8_out, R0);
  not not_9 (not_9_out, R1);
  not not_10 (not_10_out, R2);
  not not_11 (not_11_out, R3);
  not not_12 (not_12_out, C0);
  not not_13 (not_13_out, C1);
  not not_14 (not_14_out, C2);
  and and_1 (and_1_out, R0, C0);
  and and_2 (and_2_out, R0, C2);
  and and_3 (and_3_out, R1, C1);
  and and_4 (and_4_out, R2, C0);
  and and_5 (and_5_out, R2, C2);
  and and_6 (and_6_out, R3, C2);
  and and_7 (and_7_out, R0, not_2_out, not_3_out, not_4_out);
  and and_8 (and_8_out, not_1_out, R1, not_3_out, not_4_out);
  and and_9 (and_9_out, not_1_out, not_2_out, R2, not_4_out);
  and and_10 (and_10_out, not_1_out, not_2_out, not_3_out, R3);
  and and_11 (and_11_out, C0, not_6_out, not_7_out);
  and and_12 (and_12_out, not_5_out, C1, not_7_out);
  and and_13 (and_13_out, not_5_out, not_6_out, C2);
  or or_1 (B0, and_1_out, and_2_out, and_3_out, and_4_out, and_5_out, and_6_out);
  or or_2 (or_2_out, and_7_out, and_8_out, and_9_out, and_10_out);
  or or_3 (or_3_out, and_11_out, and_12_out, and_13_out);
  and and_14 (and_14_out, R0, C1);
  and and_15 (and_15_out, R0, C2);
  and and_16 (and_16_out, R1, C2);
  and and_17 (and_17_out, R2, C0);
  and and_18 (and_18_out, R3, C0);
  and and_19 (and_19_out, R3, C2);
  and and_20 (V, or_2_out, or_3_out);
  or or_4 (B1, and_14_out, and_15_out, and_16_out, and_17_out, and_18_out, and_19_out);
  and and_21 (and_21_out, R1, C0);
  and and_22 (and_22_out, R1, C1);
  and and_23 (and_23_out, R1, C2);
  and and_24 (and_24_out, R2, C0);
  or or_5 (B2, and_21_out, and_22_out, and_23_out, and_24_out);
  and and_25 (and_25_out, R2, C1);
  and and_26 (and_26_out, R2, C2);
  and and_27 (and_27_out, R3, C0);
  and and_28 (and_28_out, R3, C2);
  or or_6 (B3, and_25_out, and_26_out, and_27_out, and_28_out);
endmodule

module InputBuffer (
  input  B0,
  input  B1,
  input  B2,
  input  B3,
  input  V,
  input  CLK,
  output C0,
  output C1,
  output C2,
  output C3
);

  wire BB0, BB1, BB2, BB3, comparator_1_eq;
  wire [1:0] multiplexer_1_out, multiplexer_2_out, multiplexer_3_out, multiplexer_4_out, state_q;

  Register #(.width(1)) register_1 (.D(B0), .en(1'b1), .clk(CLK), .Q(BB0));  // open: clr
  Register #(.width(1)) register_2 (.D(B1), .en(1'b1), .clk(CLK), .Q(BB1));  // open: clr
  Register #(.width(1)) register_3 (.D(B2), .en(1'b1), .clk(CLK), .Q(BB2));  // open: clr
  Register #(.width(1)) register_4 (.D(B3), .en(1'b1), .clk(CLK), .Q(BB3));  // open: clr
  Multiplexer #(.width(2)) multiplexer_1 (.in0(2'b00), .in1(2'b01), .out(multiplexer_1_out), .sel(V));
  Multiplexer #(.width(2)) multiplexer_2 (.in0(2'b00), .in1(2'b10), .out(multiplexer_2_out), .sel(V));
  Multiplexer #(.width(2)) multiplexer_3 (.in0(2'b00), .in1(2'b10), .out(multiplexer_3_out), .sel(V));
  Multiplexer #(.select(2), .width(2)) multiplexer_4 (
    .in0(multiplexer_1_out), .in1(multiplexer_2_out), .in2(multiplexer_3_out), .out(multiplexer_4_out),
    .sel(state_q));  // open: in3
  Register #(.width(2)) state (.D(multiplexer_4_out), .en(1'b1), .clk(CLK), .Q(state_q));  // open: clr
  Comparator #(.width(2)) comparator_1 (.a(state_q), .b(2'b01), .eq(comparator_1_eq));  // open: gt, lt
  Multiplexer multiplexer_5 (.in0(1'b1), .in1(BB0), .out(C0), .sel(comparator_1_eq));
  Multiplexer multiplexer_6 (.in0(1'b1), .in1(BB1), .out(C1), .sel(comparator_1_eq));
  Multiplexer multiplexer_7 (.in0(1'b1), .in1(BB2), .out(C2), .sel(comparator_1_eq));
  Multiplexer multiplexer_8 (.in0(1'b1), .in1(BB3), .out(C3), .sel(comparator_1_eq));
endmodule

module Lock (
  input  C0,
  input  C1,
  input  C2,
  input  C3,
  input  CLK,
  output L,
  output U
);

  wire and_3_out, comparator_1_eq, comparator_2_eq, comparator_9_eq, comparator_11_eq, comparator_12_eq,
       comparator_13_eq, Lcode, LockingFin, not_1_out, not_2_out, not_3_out, not_4_out, not_5_out, not_6_out,
       or_1_out, Othercode, TopLock, TopUnlock, Ucode, UD0, UD1, UD2, UFin, UI0, UI1, UI2, UPASSWD;
  wire [1:0] adder_1_out, multiplexer_4_out, multiplexer_5_out, multiplexer_6_out, multiplexer_7_out,
       multiplexer_12_out, multiplexer_13_out, register_1_q, TopState;
  wire [2:0] LockState_q, multiplexer_1_out, multiplexer_2_out, multiplexer_3_out, multiplexer_8_out,
       multiplexer_9_out, multiplexer_10_out, multiplexer_11_out, multiplexer_14_out, multiplexer_15_out,
       multiplexer_16_out, multiplexer_17_out, multiplexer_18_out, multiplexer_19_out, multiplexer_20_out,
       multiplexer_21_out, multiplexer_22_out, UnlockState_q;
  wire [3:0] D0, D1, D2, I0, I1, I2, P0, P1, P2;

  Multiplexer #(.width(3)) multiplexer_1 (.in0(3'b000), .in1(3'b011), .out(multiplexer_1_out), .sel(Othercode));
  Multiplexer #(.width(3)) multiplexer_2 (.in0(3'b000), .in1(3'b100), .out(multiplexer_2_out), .sel(Othercode));
  Multiplexer #(.width(3)) multiplexer_3 (.in0(3'b000), .in1(3'b101), .out(multiplexer_3_out), .sel(Othercode));
  Multiplexer #(.width(2)) multiplexer_4 (.in0(2'b00), .in1(2'b01), .out(multiplexer_4_out), .sel(TopLock));
  Multiplexer #(.width(2)) multiplexer_5 (.in0(2'b01), .in1(2'b10), .out(multiplexer_5_out), .sel(LockingFin));
  Multiplexer #(.width(2)) multiplexer_6 (.in0(2'b10), .in1(2'b11), .out(multiplexer_6_out), .sel(TopUnlock));
  Multiplexer #(.width(2)) multiplexer_7 (.in0(2'b11), .in1(2'b00), .out(multiplexer_7_out), .sel(LockingFin));
  Comparator #(.width(2)) comparator_1 (.a(TopState), .b(2'b01), .eq(comparator_1_eq));  // open: gt, lt
  Comparator #(.width(2)) comparator_2 (.a(TopState), .b(2'b11), .eq(comparator_2_eq));  // open: gt, lt
  Multiplexer #(.width(3)) multiplexer_8 (.in0(3'b000), .in1(3'b001), .out(multiplexer_8_out), .sel(Lcode));
  Multiplexer #(.width(3)) multiplexer_9 (.in0(multiplexer_1_out), .in1(3'b010), .out(multiplexer_9_out), .sel(Lcode));
  Multiplexer #(.width(3)) multiplexer_10 (
    .in0(multiplexer_2_out), .in1(3'b001), .out(multiplexer_10_out), .sel(Lcode));
  Multiplexer #(.width(3)) multiplexer_11 (
    .in0(multiplexer_3_out), .in1(3'b001), .out(multiplexer_11_out), .sel(Lcode));
  Multiplexer #(.width(2)) multiplexer_12 (.in0(2'b00), .in1(adder_1_out), .out(multiplexer_12_out), .sel(or_1_out));
  or or_1 (or_1_out, comparator_1_eq, comparator_2_eq);
  Register #(.width(2)) TopLevelState (.D(multiplexer_13_out), .en(1'b1), .clk(CLK), .Q(TopState));  // open: clr
  Multiplexer #(.select(2), .width(2)) multiplexer_13 (
    .in0(multiplexer_4_out), .in1(multiplexer_5_out), .in2(multiplexer_6_out), .in3(multiplexer_7_out),
    .out(multiplexer_13_out), .sel(TopState));
  Register #(.width(2)) register_1 (.D(multiplexer_12_out), .en(1'b1), .clk(CLK), .Q(register_1_q));  // open: clr
  Comparator #(.width(2)) comparator_3 (.a(TopState), .b(2'b01), .eq(L));  // open: gt, lt
  Comparator #(.width(2)) comparator_4 (.a(TopState), .b(2'b11), .eq(U));  // open: gt, lt
  Register #(.width(3)) LockState (.D(multiplexer_14_out), .en(1'b1), .clk(CLK), .Q(LockState_q));  // open: clr
  Multiplexer #(.select(3), .width(3)) multiplexer_14 (
    .in0(multiplexer_8_out), .in1(multiplexer_9_out), .in2(3'b000), .in3(multiplexer_10_out),
    .in4(multiplexer_11_out), .in5(3'b000), .out(multiplexer_14_out), .sel(LockState_q));  // open: in6, in7
  Register #(.width(4)) digit1 (.D({C3, C2, C1, C0}), .en(UD0), .clk(CLK), .Q(D0));  // open: clr
  Register #(.width(4)) PWD0 (.D(D0), .en(UPASSWD), .clk(CLK), .Q(P0));  // open: clr
  Adder #(.width(2)) adder_1 (.a(register_1_q), .b(2'b01), .out(adder_1_out));  // open: cin, cout
  Comparator #(.width(2)) comparator_5 (.a(register_1_q), .b(2'b11), .eq(LockingFin));  // open: gt, lt
  Register #(.width(4)) digit2 (.D({C3, C2, C1, C0}), .en(UD1), .clk(CLK), .Q(D1));  // open: clr
  Register #(.width(4)) PWD1 (.D(D1), .en(UPASSWD), .clk(CLK), .Q(P1));  // open: clr
  not not_1 (not_1_out, C0);
  not not_2 (not_2_out, C2);
  not not_3 (not_3_out, C2);
  Comparator #(.width(3)) comparator_6 (.a(3'b001), .b(LockState_q), .eq(UD0));  // open: gt, lt
  Comparator #(.width(3)) comparator_7 (.a(3'b011), .b(LockState_q), .eq(UD1));  // open: gt, lt
  Comparator #(.width(3)) comparator_8 (.a(3'b100), .b(LockState_q), .eq(UD2));  // open: gt, lt
  Comparator #(.width(3)) comparator_9 (.a(LockState_q), .b(3'b010), .eq(comparator_9_eq));  // open: gt, lt
  Comparator #(.width(3)) comparator_10 (.a(LockState_q), .b(3'b101), .eq(UPASSWD));  // open: gt, lt
  and and_1 (Lcode, not_1_out, C1, not_2_out, C3);
  and and_2 (Ucode, C0, C1, not_3_out, C3);
  and and_3 (and_3_out, C0, C1, C2, C3);
  or or_2 (TopLock, comparator_9_eq, UPASSWD);
  Register #(.width(4)) digit3 (.D({C3, C2, C1, C0}), .en(UD2), .clk(CLK), .Q(D2));  // open: clr
  Register #(.width(4)) PWD2 (.D(D2), .en(UPASSWD), .clk(CLK), .Q(P2));  // open: clr
  not not_4 (not_4_out, and_3_out);
  not not_5 (not_5_out, Ucode);
  not not_6 (not_6_out, Lcode);
  and and_4 (Othercode, not_4_out, not_5_out, not_6_out);
  Multiplexer #(.width(3)) multiplexer_15 (.in0(3'b010), .in1(3'b000), .out(multiplexer_15_out), .sel(Lcode));
  Multiplexer #(.width(3)) multiplexer_16 (.in0(3'b011), .in1(3'b000), .out(multiplexer_16_out), .sel(Lcode));
  Multiplexer #(.width(3)) multiplexer_17 (.in0(3'b100), .in1(3'b000), .out(multiplexer_17_out), .sel(Lcode));
  Multiplexer #(.width(3)) multiplexer_18 (.in0(3'b000), .in1(3'b001), .out(multiplexer_18_out), .sel(Ucode));
  Multiplexer #(.width(3)) multiplexer_19 (
    .in0(multiplexer_15_out), .in1(3'b001), .out(multiplexer_19_out), .sel(Ucode));
  Multiplexer #(.width(3)) multiplexer_20 (
    .in0(multiplexer_16_out), .in1(3'b001), .out(multiplexer_20_out), .sel(Ucode));
  Multiplexer #(.width(3)) multiplexer_21 (
    .in0(multiplexer_17_out), .in1(3'b001), .out(multiplexer_21_out), .sel(Ucode));
  Register #(.width(4)) register_2 (.D({C3, C2, C1, C0}), .en(UI0), .clk(CLK), .Q(I0));  // open: clr
  Comparator #(.width(4)) comparator_11 (.a(I0), .b(D0), .eq(comparator_11_eq));  // open: gt, lt
  Comparator #(.width(4)) comparator_12 (.a(I1), .b(D1), .eq(comparator_12_eq));  // open: gt, lt
  Comparator #(.width(4)) comparator_13 (.a(I2), .b(D2), .eq(comparator_13_eq));  // open: gt, lt
  Multiplexer #(.select(3), .width(3)) multiplexer_22 (
    .in0(multiplexer_18_out), .in1(multiplexer_19_out), .in2(multiplexer_20_out), .in3(multiplexer_21_out),
    .in4(3'b000), .out(multiplexer_22_out), .sel(UnlockState_q));  // open: in5, in6, in7
  and and_5 (TopUnlock, UFin, comparator_11_eq, comparator_12_eq, comparator_13_eq);
  Register #(.width(3)) UnlockState (.D(multiplexer_22_out), .en(1'b1), .clk(CLK), .Q(UnlockState_q));  // open: clr
  Register #(.width(4)) register_3 (.D({C3, C2, C1, C0}), .en(UI1), .clk(CLK), .Q(I1));  // open: clr
  Register #(.width(4)) register_4 (.D({C3, C2, C1, C0}), .en(UI2), .clk(CLK), .Q(I2));  // open: clr
  Comparator #(.width(3)) comparator_14 (.a(3'b001), .b(UnlockState_q), .eq(UI0));  // open: gt, lt
  Comparator #(.width(3)) comparator_15 (.a(3'b010), .b(UnlockState_q), .eq(UI1));  // open: gt, lt
  Comparator #(.width(3)) comparator_16 (.a(3'b011), .b(UnlockState_q), .eq(UI2));  // open: gt, lt
  Comparator #(.width(3)) comparator_17 (.a(3'b100), .b(UnlockState_q), .eq(UFin));  // open: gt, lt

  // Other names for the same wires on the sheet: UnlockingFin = LockingFin
endmodule
